// Logisim project processor.circ as structural Verilog: 2 circuits, main circuit processor
// decoder
module decode (
  input  [31:0] in_1,
  output [4:0] rd,
  output [6:0] funct7,
  output [2:0] funct3,
  output [4:0] rs1,
  output [4:0] rs2,
  output r,
  output i,
  output [11:0] imm,
  output s,
  output sb
);

  wire [2:0] and_1_out_2, and_2_out_2;
  wire [3:0] and_4_out_2;
  wire [4:0] and_1_out, and_1_out_3, and_1_out_4, and_2_out, and_2_out_3;
  wire [5:0] and_4_out_3;
  wire [11:0] and_2_out_4, and_3_out_2;
  wire [11:10] and_4_out_4;
  wire [17:5] and_3_out, and_4_out;
  wire [24:0] bit_extender_1_out, bit_extender_2_out, bit_extender_3_out, bit_extender_4_out;

  and rtype (r, in_1[0], in_1[1], ~in_1[2], ~in_1[3], in_1[4], in_1[5], ~in_1[6]);  // AND_Gate
  and itype (i, in_1[0], in_1[1], ~in_1[2], ~in_1[3], in_1[4], ~in_1[5], ~in_1[6]);  // AND_Gate
  and stype (s, in_1[0], in_1[1], ~in_1[2], ~in_1[3], ~in_1[4], in_1[5], ~in_1[6]);  // AND_Gate
  and sbtype (sb, in_1[0], in_1[1], ~in_1[2], ~in_1[3], ~in_1[4], in_1[5], in_1[6]);  // AND_Gate
  assign bit_extender_1_out = {{24{r}}, r};  // Bit_Extender bit_extender_1
  assign bit_extender_2_out = {{24{i}}, i};  // Bit_Extender bit_extender_2
  assign bit_extender_3_out = {{24{s}}, s};  // Bit_Extender bit_extender_3
  assign bit_extender_4_out = {{24{sb}}, sb};  // Bit_Extender bit_extender_4
  assign {funct7, and_1_out_4, and_1_out_3, and_1_out_2, and_1_out} = bit_extender_1_out & in_1[31:7];  // AND_Gate and_1, 25 bits wide
  assign {and_2_out_4, and_2_out_3, and_2_out_2, and_2_out} = bit_extender_2_out & in_1[31:7];  // AND_Gate and_2, 25 bits wide
  assign {and_3_out_2[11:5], and_3_out, and_3_out_2[4:0]} = bit_extender_3_out & in_1[31:7];  // AND_Gate and_3, 25 bits wide
  assign {and_4_out_4[11], and_4_out_3, and_4_out, and_4_out_2, and_4_out_4[10]} = bit_extender_4_out & in_1[31:7];  // AND_Gate and_4, 25 bits wide
  assign rd = and_1_out | and_2_out;  // OR_Gate or_1, 5 bits wide
  assign funct3 = and_1_out_2 | and_2_out_2 | and_3_out[7:5] | and_4_out[7:5];  // OR_Gate or_2, 3 bits wide
  assign rs1 = and_1_out_3 | and_2_out_3 | and_3_out[12:8] | and_4_out[12:8];  // OR_Gate or_3, 5 bits wide
  assign rs2 = and_1_out_4 | and_3_out[17:13] | and_4_out[17:13];  // OR_Gate or_4, 5 bits wide
  assign imm = and_2_out_4 | and_3_out_2 | {and_4_out_4, and_4_out_3, and_4_out_2};  // OR_Gate or_5, 12 bits wide
endmodule

module processor (
  input  [31:0] in_1
);

  wire clk, i, r, s, sb, undriven_2;
  wire [2:0] f3;
  wire [3:0] undriven_3;
  wire [4:0] rd, rs1, rs2;
  wire [6:0] f7;
  wire [11:0] imm;
  wire [31:0] instr, multiplexer_1_out, regfile_1_rd1, regfile_1_rd2, undriven;

  Clock clock_1 (.out(clk));
  decode decode_1 (
    .in_1(instr), .rd(rd), .funct3(f3), .rs1(rs1), .rs2(rs2), .imm(imm), .funct7(f7), .sb(sb), .s(s), .i(i),
    .r(r));
  regfile regfile_1 (.clk(clk), .rd1(regfile_1_rd1), .rd2(regfile_1_rd2));  // open: rs2, rd, rs1, wd, RegWEn
  Multiplexer #(.enable("true"), .width(32)) multiplexer_1 (
    .in0(undriven), .in1(regfile_1_rd2), .out(multiplexer_1_out), .sel(undriven_2));  // open: en
  alu alu_1 (.A(regfile_1_rd1), .ALUSel(undriven_3), .B(multiplexer_1_out));  // open: OverFlow, Result, Zero
endmodule
